// Logisim project fpadder.circ as structural Verilog: 1 circuit, main circuit main
module main (
  input  in_1,
  input  [15:0] in_2,
  input  [15:0] in_3,
  input  [3:0] in_4,
  input  [15:0] in_5,
  input  in_6,
  input  [15:0] in_7,
  input  [15:0] in_8,
  input  [15:0] in_9,
  input  [3:0] in_10,
  input  in_11,
  input  [15:0] in_12,
  input  [15:0] in_13,
  input  [3:0] in_14,
  input  [3:0] in_15,
  input  [3:0] in_16,
  input  [3:0] in_17,
  input  in_18,
  input  in_19,
  input  in_20,
  output [15:0] out_21,
  output out_22,
  output [3:0] out_23,
  output [3:0] out_24,
  output [3:0] out_25
);

  wire and_1_out, not_1_out, not_2_out, not_3_out, not_4_out, subtractor_1_bout, xor_1_out;
  wire [3:0] multiplexer_4_out, subtractor_1_out;
  wire [15:0] adder_2_out, adder_3_out, adder_4_out, multiplexer_2_out, multiplexer_3_out, multiplexer_5_out,
       or_1_out, or_2_out, shifter_1_out, shifter_2_out, shifter_3_out, xor_3_out, xor_4_out;

  Subtractor #(.width(4)) subtractor_1 (
    .a(in_14), .b(in_15), .out(subtractor_1_out), .bin(in_11), .bout(subtractor_1_bout));
  xor xor_1 (xor_1_out, in_19, in_20);
  Shifter #(.width(16), .shift("lr")) shifter_1 (.in(in_3), .\dist (in_4), .out(shifter_1_out));
  Shifter #(.width(16), .shift("lr")) shifter_2 (.in(in_5), .\dist (in_10), .out(shifter_2_out));
  assign out_23 = subtractor_1_out ^ in_17;  // XOR_Gate xor_2, 4 bits wide
  Multiplexer #(.width(4)) multiplexer_1 (.in0(in_14), .in1(in_15), .out(out_25), .sel(subtractor_1_bout), .en(in_18));
  assign or_1_out = shifter_1_out | in_2;  // OR_Gate or_1, 16 bits wide
  assign or_2_out = shifter_2_out | in_9;  // OR_Gate or_2, 16 bits wide
  Adder #(.width(4)) adder_1 (.a(out_23), .b(in_16), .out(out_24));  // open: cin, cout
  Multiplexer #(.width(16)) multiplexer_2 (
    .in0(or_1_out), .in1(or_2_out), .out(multiplexer_2_out), .sel(not_2_out), .en(in_6));
  not not_1 (not_1_out, not_2_out);
  not not_2 (not_2_out, subtractor_1_bout);
  Multiplexer #(.width(16)) multiplexer_3 (
    .in0(or_1_out), .in1(or_2_out), .out(multiplexer_3_out), .sel(not_1_out), .en(in_6));
  Multiplexer #(.width(4)) multiplexer_4 (
    .in0(subtractor_1_out), .in1(out_24), .out(multiplexer_4_out), .sel(subtractor_1_bout), .en(in_18));
  Shifter #(.width(16), .shift("lr")) shifter_3 (
    .in(multiplexer_2_out), .\dist (multiplexer_4_out), .out(shifter_3_out));
  assign xor_3_out = shifter_3_out ^ in_12;  // XOR_Gate xor_3, 16 bits wide
  Adder #(.width(16)) adder_2 (.a(xor_3_out), .b(in_13), .out(adder_2_out));  // open: cin, cout
  Multiplexer #(.width(16)) multiplexer_5 (
    .in0(shifter_3_out), .in1(adder_2_out), .out(multiplexer_5_out), .sel(xor_1_out), .en(in_18));
  Adder #(.width(16)) adder_3 (
    .a(multiplexer_3_out), .b(multiplexer_5_out), .out(adder_3_out), .cin(in_1), .cout(out_22));
  not not_3 (not_3_out, out_22);
  assign xor_4_out = adder_3_out ^ in_7;  // XOR_Gate xor_4, 16 bits wide
  Adder #(.width(16)) adder_4 (.a(xor_4_out), .b(in_8), .out(adder_4_out));  // open: cin, cout
  not not_4 (not_4_out, xor_1_out);
  buf and_1 (and_1_out, not_4_out);  // AND_Gate
  Multiplexer #(.width(16)) multiplexer_6 (
    .in0(adder_3_out), .in1(adder_4_out), .out(out_21), .sel(and_1_out), .en(in_18));

  // Notes on the sheet:
  //                       Exponents
  //   Exponent diff
  //                     Resulting exp
  //   Shift right
  //   Control for small exp
endmodule
